# Fritzing sketch Garduino (saved by Fritzing 0.9.3b)
breadboards: 1

parts:
  Part1 = Arduino Uno (Rev3) - ICSP
  T1 = LM35 Temperature Sensor [package="TO92 [THT]"]
  R1 = PHOTOCELL [package=photocell-kit]
  R2 = Resistor [tolerance=±5% resistance=10k package=THT]
  Part5 = FC-28 Soil Hygrometer Module [part_number=YL-38]
  Part6 = FC-28 Soil Hygrometer Module - Probe [part_number=YL-69]

nets:
  N1: Part1.A0, Part5.AO
  N2: Part1.A3, T1.Vout
  N3: Part1.A5/SCL, R1.P$2, R2.Pin_0
  5V: Part1.5V, T1.+Vs, R1.P$1, Part5.VCC
  GND: Part1.GND, T1.GND, R2.Pin_1, Part5.GND
  N4: Part5.POS, Part6.POS
  N5: Part5.NEG, Part6.NEG

custom parts:
  FC-28 Soil Hygrometer Module: The FC-28 is a soil hygrometer module that uses the Texas Instruments LM393 comparator chip to provide an analog measurement of soil humidity. The digital output is high when soil moisture is over a certain threshold, as determined by adjusting the potentiometer.
  FC-28 Soil Hygrometer Module - Probe: The FC-28 is a soil hygrometer module that uses the Texas Instruments LM393 comparator chip to provide an analog measurement of soil humidity.
